# Fritzing sketch plarail_train_esp32 (saved by Fritzing 0.9.10b)

parts:
  ESP32_-_Back1 = ESP32 - CAM
  U1 = L9110 H-bridge module [part_number="L9110 H-bridge"]
  M1 = DC Motor [voltage_(max)=6V voltage_(min)=3V]
  U2 = LIPO-2000mAh [package=lipo-2000]

nets:
  N1: ESP32_-_Back1.GPIO13, U1.A-IB
  N2: ESP32_-_Back1.GPIO12, U1.A-IA
  N3: ESP32_-_Back1.GND#7, U2.-
  N4: ESP32_-_Back1.5V, U2.+
  N5: ESP32_-_Back1.GND#12, U1.GND
  N6: ESP32_-_Back1.3.3V_/_5V_/_P_OUT, U1.VCC
  N7: U1.MOTOR_A-A, M1.pin_2
  N8: U1.MOTOR_A-B, M1.pin_1

custom parts:
  ESP32 - CAM: The ESP32-CAM has a very competitive small-size camera module that can operate independently as a minimum system with a footprint of only 27*40.5*4.5mm and a deep sleep current of up to 6mA.
